# Fritzing sketch kadai7sg_fin (saved by Fritzing 0.9.2b)
breadboards: 1

parts:
  パーツ1 = Arduino Mega 2560 (Rev3)
  R1 = Resistor [tolerance=±5% resistance=220 package=THT]
  R2 = Resistor [tolerance=±5% resistance=220 package=THT]
  R3 = Resistor [tolerance=±5% resistance=220 package=THT]
  R4 = Resistor [tolerance=±5% resistance=220 package=THT]
  R5 = Resistor [tolerance=±5% resistance=220 package=THT]
  R6 = Resistor [tolerance=±5% resistance=220 package=THT]
  R7 = Resistor [tolerance=±5% resistance=220 package=THT]

nets:
  N1: パーツ1.D8_PWM, R2.Pin_1
  N2: パーツ1.D2_PWM, R1.Pin_1
  N3: パーツ1.D3_PWM, R7.Pin_1
  N4: パーツ1.D4_PWM, R6.Pin_1
  N5: パーツ1.D5_PWM, R5.Pin_1
  N6: パーツ1.D6_PWM, R4.Pin_1
  N7: パーツ1.D7_PWM, R3.Pin_1
